# Fritzing sketch Esquetepingpong (saved by Fritzing 0.9.3b)
breadboards: 1

parts:
  Componente1 = Arduino Uno (Rev3)
  R1 = Resistor [tolerance=±5% resistance=10k package=THT]  # not connected
  S1 = Pushbutton [package="[THT]"]
  S2 = Pushbutton [package="[THT]"]
  R2 = Resistor [tolerance=±5% resistance=10k package=THT]  # not connected
  Componente2 = LED Matrix - Serial Interface - Red/Green/Blue

nets:
  N1: Componente1.D8, S1.Pin_1, S1.Pin_2
  N2: Componente1.D2, Componente2.SCK
  N3: Componente1.D3_PWM, Componente2.CS
  N4: Componente1.D4, Componente2.MOSI
  N5: Componente1.D7, S2.Pin_3, S2.Pin_4
  N6: Componente1.3V3, S1.Pin_3, S1.Pin_4, S2.Pin_1, S2.Pin_2
  5V: Componente1.5V, Componente2.VCC

notes:
  MATRIX LED
  VCC=5V
  GND=QUALQUER UM
  DIN=PORTA DIGITAL 2
  CLK=PORTA DIGITAL 3
  CS=PORTA DIGITAL 4
  BUTTONS
  PORTA DIGITAIS 7 E 8
  SEGUIR O ESQUEMA NÃO TEM ERRO
